# Fritzing sketch connection_diagram_schem_0.2 (saved by Fritzing 0.8.5b)
circuit board: 9.88247cm x 7.56655cm
breadboards: 1

parts:
  V2 = DC Power [voltage=5V]
  R10k = 20 kΩ Resistor [package=THT]
  C15nF = Ceramic Capacitor 15 nF [package="1206 [SMD, multilayer]"]
  C15nF_2 = Ceramic Capacitor 15 nF [package="1206 [SMD, multilayer]"]
  C = Ceramic Capacitor [capacitance="100 nF" package="0805 [SMD, multilayer]"]
  U3 = atmega328_jo [package=dip]
  LCD1 = LCD screen
  VR10kB_LCD_Contrast = Trimmer Potentiometer [maximum_resistance=10kΩ package=THT]
  C_2 = Electrolytic Capacitor [capacitance=100µF package="200 mil [THT, electrolytic]"]
  XTAL_12_Mhz = Crystal [package=SMD]
  VR100kB_ADC_Input_Potmeter = POT [package=pot_alpha_rv16af-20]
  Power_Source_Socket = Header 3 [package=screwterminal-3.5mm-3_lock.007s]
  Servo_Socket = Header 3 [package=screwterminal-3.5mm-3_lock.007s]
  ISP_header = AVR ISP 6 Pin_jo [package=2x3]
  SW_RIGHT = Momentary Switch [package=tactile-pth]
  built-in_LED_green = LTE-302 [package=lte-302]
  SW_OK = Momentary Switch [package=tactile-pth]
  built-in_LED_green_2 = LTE-302 [package=lte-302]
  SW_LEFT = Momentary Switch [package=tactile-pth]
  built-in_LED_green_3 = LTE-302 [package=lte-302]
  SW_UP = Momentary Switch [package=tactile-pth]
  built-in_LED_green_4 = LTE-302 [package=lte-302]
  SW_DOWN = Momentary Switch [package=tactile-pth]
  built-in_LED_green_5 = LTE-302 [package=lte-302]
  SW_NA = SWITCH_SPDT [package=kps-1290]
  built-in_LED_red = LTE-302 [package=lte-302]
  R390Ω = 390Ω Resistor [package=THT]
  R390Ω_2 = 390Ω Resistor [package=THT]
  R390Ω_3 = 390Ω Resistor [package=THT]
  R390Ω_4 = 390Ω Resistor [package=THT]
  R390Ω_5 = 390Ω Resistor [package=THT]
  R390Ω_6 = 390Ω Resistor [package=THT]

nets:
  +5V: V2.V+, R10k.Pin_1, C.1, U3.VCC, U3.AVCC, U3.AREF, LCD1.VDD, VR10kB_LCD_Contrast.leg1, C_2.+, VR100kB_ADC_Input_Potmeter.E, Power_Source_Socket.+5V, Servo_Socket.+5V, ISP_header.2/VCC, R390Ω.Pin_1, R390Ω_2.Pin_1, R390Ω_3.Pin_1, R390Ω_4.Pin_1, R390Ω_5.Pin_1
  N1: R10k.Pin_0, U3.PC6/RESET, ISP_header.5/nRESET
  GND: C15nF.0, C15nF_2.0, C.0, U3.GND, LCD1.VSS, VR10kB_LCD_Contrast.leg2, C_2.-, VR100kB_ADC_Input_Potmeter.A, Power_Source_Socket.GND, Servo_Socket.GND, ISP_header.6/GND, SW_RIGHT.4, built-in_LED_green.C, SW_OK.4, built-in_LED_green_2.C, SW_LEFT.4, built-in_LED_green_3.C, SW_UP.4, built-in_LED_green_4.C, SW_DOWN.4, built-in_LED_green_5.C, SW_NA.P, built-in_LED_red.C
  N2: C15nF.1, U3.PB6/XLAT1, XTAL_12_Mhz.pin_0
  N3: C15nF_2.1, U3.PB7/XLAT2, XTAL_12_Mhz.pin_1
  N4: U3.PD0/RX, LCD1.DB4
  N5: U3.PD1/TX, LCD1.DB5
  N6: U3.PD2, LCD1.DB6
  N7: U3.PD3/OC2B/MOSI, LCD1.DB7
  N8: U3.PD4, LCD1.E
  N9: U3.PD5/OC0B/T1, LCD1.R/W
  N10: U3.PD6/OC0A, LCD1.RS
  N11: U3.PD7, R390Ω_6.Pin_1
  N12: U3.PB0, Power_Source_Socket.Signal
  N13: U3.PB1/OC1A, SW_NA.S
  N14: U3.PB2/OC1B, Servo_Socket.Signal
  N15: U3.PB3/OC2A, ISP_header.4/MOSI, SW_DOWN.2
  N16: U3.PB4/MISO, ISP_header.1/MISO, SW_UP.2
  N17: U3.PB5/SCK, ISP_header.3/SCK, SW_LEFT.2
  N18: U3.PC0/ADC0, VR100kB_ADC_Input_Potmeter.S
  N19: U3.PC4/ADC4/, SW_OK.2
  N20: U3.PC5/ADC5, SW_RIGHT.2
  N21: LCD1.V0, VR10kB_LCD_Contrast.wiper
  N22: built-in_LED_green.A, R390Ω_3.Pin_0
  N23: built-in_LED_green_2.A, R390Ω_4.Pin_0
  N24: built-in_LED_green_3.A, R390Ω_5.Pin_0
  N25: built-in_LED_green_4.A, R390Ω_2.Pin_0
  N26: built-in_LED_green_5.A, R390Ω.Pin_0
  N27: built-in_LED_red.A, R390Ω_6.Pin_0

custom parts:
  20 kΩ Resistor: A generic 5-band resistor (0.25W)
  Ceramic Capacitor 15 nF: 15 nF Ceramic Capacitor
  atmega328_jo: Atmel ATmega328 microcontroller.
  Header 3: Header 3 Standard 3-pin 0.1 header. Use with straight break away headers (SKU : PRT-00116), right angle break away headers (PRT-00553), swiss pins (PRT-00743), machine pins (PRT-00117), and female headers (PRT-00115). Molex polarized connector foot print use with SKU : PRT-08232 with associated crimp pins and housings.
  AVR ISP 6 Pin_jo: AVR ISP 6 Pin This is the reduced ISP connector for AVR programming. Common on Arduino. This footprint will take up less PCB space and can be used with a 10-pin to 6-pin adapter such as SKU: BOB-08508
  390Ω Resistor: A generic 5-band resistor (0.25W)
